# Fritzing sketch Angular (saved by Fritzing 0.9.5d)

parts:
  part = Arduino Nano (Rev3.0)
  S1 = Toggle Switch [package=THT]
  MAX7219 = MAX7219 v2
  ADXL345 = Triple Axis Accelerometer Breakout - ADXL345
  MT3608 = MT3608 Boost No usb
  part_2 = TP4056 [chip_label=TP4056 package="DIP (Dual Inline) [THT]"]
  BAT = LIPO-1000mAh [package=lipo-1000]

nets:
  GND: part.GND, MAX7219.GND, ADXL345.GND, MT3608.IN_(-), MT3608.OUT_(-), part_2.pin5, BAT.-
  N1: part.D5, MAX7219.CS
  N2: part.D11/MOSI, MAX7219.DIN
  VCC: part.5V, S1.COM, MAX7219.VCC, ADXL345.VCC
  N3: part.A5, ADXL345.SCL
  N4: part.A4, ADXL345.SDA
  N5: part.D13/SCK, MAX7219.CLK
  N6: S1.L2, MT3608.OUT_(+)
  N7: MT3608.IN_(+), part_2.pin4, BAT.+

custom parts:
  MT3608 Boost No usb: Chip- MT3608 / B6289 DC to DC step up, power booster module. With adjustable output voltage. Current- 2A . || Input voltage- 2V-24V || Output voltage- 5V-28V Input interface- Inversed polarity- NO. || Led indicator- No.
  TP4056: A DIP stand-in part for whatever IC you want. With 6 pins on a 300mil dual inline package (DIP) footprint.
